// Logisim project Dom2.circ as structural Verilog: 1 circuit, main circuit Dom2
module Dom2 (
  input  in_1,
  input  in_2,
  input  in_3,
  input  in_4,
  input  in_5,
  output out_6
);

  wire nor_1_out, nor_2_out, nor_3_out, nor_4_out, nor_5_out, nor_6_out, nor_7_out, nor_8_out;

  nor nor_1 (nor_1_out, in_3, in_3);
  nor nor_2 (nor_2_out, in_1, in_2);
  nor nor_3 (nor_3_out, in_4, in_4);
  nor nor_4 (nor_4_out, nor_2_out, nor_2_out);
  nor nor_5 (nor_5_out, nor_3_out, in_5);
  nor nor_6 (nor_6_out, nor_4_out, nor_1_out);
  nor nor_7 (nor_7_out, nor_5_out, nor_5_out);
  nor nor_8 (nor_8_out, nor_6_out, nor_6_out);
  nor nor_9 (out_6, nor_8_out, nor_7_out);

  // Notes on the sheet:
  //   01.05.
endmodule
